# Fritzing sketch MovementSensor (saved by Fritzing 0.9.2b)

parts:
  Součástka1 = Arduino Uno (Rev3)
  PIR1 = PIR_sensor

nets:
  N1: Součástka1.D7, PIR1.connector2
  N2: Součástka1.5V, PIR1.connector1
  N3: Součástka1.GND, PIR1.connector3
